# Fritzing sketch HW2P3 (saved by Fritzing 0.9.3b)

parts:
  Part2 = LilyPad Arduino Simple Board
  Part3 = LilyPad LED
  Part4 = LilyPad LED
  Part5 = LilyPad Light Sensor
  Part6 = LilyPad Button Board
  Part7 = LilyPad Buzzer

nets:
  N1: Part2.A4, Part7.+
  N2: Part2.A5, Part6.S
  N3: Part2.D11, Part5.S
  N4: Part2.D6, Part3.+
  N5: Part2.D9, Part4.+
  N6: Part2.GND, Part3.-, Part4.-, Part5.-, Part6.-, Part7.-
  N7: Part2.VCC, Part5.+

notes:
  LED-D6
  Check input from Light Sensor
  If darkLimit reached
  Then LED on
  Else LED off
  LED-D9
  Check input pullup from Btn-D19
  If btn pushed
  Then LED on
  Else LED off [when btn released]
